// Logisim project component-declaration.circ as structural Verilog: 1 circuit, main circuit main
module main (
);

  wire button_1_out, button_2_out, s_r_ff_1_q, s_r_ff_1_qn;

  Button button_1 (.out(button_1_out));
  Button button_2 (.out(button_2_out));
  S_R_Flip_Flop s_r_ff_1 (
    .S(button_1_out), .R(button_2_out), .Q(s_r_ff_1_q), .Qn(s_r_ff_1_qn));  // open: clk, preset, reset, en
  LED led_1 (.in(s_r_ff_1_q));
  LED led_2 (.in(s_r_ff_1_qn));

  // Notes on the sheet:
  //   in1
  //   in2
  //   SR
  //   out1
  //   out2
endmodule
