// Logisim project error-message.circ as structural Verilog: 1 circuit, main circuit main
module main (
);

  wire button_1_out, button_2_out, not_1_out, not_2_out, or_1_out, or_2_out;

  Button button_1 (.out(button_1_out));
  Button button_2 (.out(button_2_out));
  or or_1 (or_1_out, button_1_out, button_2_out);
  LED led_1 (.in(or_1_out));
  not not_1 (not_1_out, or_1_out);
  or or_2 (or_2_out, not_1_out, not_2_out);
  LED led_2 (.in(or_2_out));
  not not_2 (not_2_out, or_2_out);

  // Notes on the sheet:
  //   in1
  //   in2
  //   or1
  //   out1
  //   not1
  //   or2
  //   out2
  //   not2
endmodule
